// Logisim project EASY WAY OUT FOR HARD PROBLEMS.circ as structural Verilog: 1 circuit, main circuit main
module main (
  input  x,
  input  y,
  input  z,
  output out_4
);

  Multiplexer #(.select(3), .enable("false")) multiplexer_1 (
    .in0(1'b0), .in1(1'b0), .in2(1'b1), .in3(1'b1), .in4(1'b1), .in5(1'b1), .in6(1'b0), .in7(1'b1),
    .out(out_4), .sel({x, y, z}));
endmodule
