// Logisim project Examplee.circ as structural Verilog: 1 circuit, main circuit main
module main (
  input  A,
  input  in_2,
  input  B,
  input  S_prime,
  input  R_prime,
  output a_2,
  output out_7,
  output a_prime,
  output a_b__prime,
  output out_10,
  output a_b_prime,
  output Q,
  output out_13
);

  wire and_1_out, clock_1_out;

  buf buffer_1 (a_2, A);
  not not_1 (a_prime, A);
  nand nand_1 (a_b__prime, A, B);
  not not_2 (a_b_prime, and_1_out);
  buf and_1 (and_1_out, A);  // AND_Gate
  nand nand_2 (Q, S_prime, out_13);
  nand nand_3 (out_13, R_prime, Q);
  Clock clock_1 (.out(clock_1_out));
  D_Flip_Flop d_ff_1 (.clk(clock_1_out), .D(in_2), .Q(out_7));  // open: Qn, preset, en, reset
  T_Flip_Flop t_ff_1 (.clk(clock_1_out), .T(in_2), .Q(out_10));  // open: Qn, preset, reset, en

  // Notes on the sheet:
  //   Sequential Logic
  //   S'R' Latch
  //   1 Bit Memory
endmodule
