// Logisim project FullAdder.circ as structural Verilog: 1 circuit, main circuit main
module main (
  input  Cin,
  input  A,
  input  B,
  input  Cin_2,
  input  A_2,
  input  B_2,
  output Carry,
  output Sum
);

  wire not_1_out;

  not not_1 (not_1_out, Cin_2);
  Multiplexer #(.select(2), .disabled(0), .enable("false")) multiplexer_1 (
    .in0(1'b0), .in1(Cin), .in2(Cin), .in3(1'b1), .out(Carry), .sel({B, A}));
  Multiplexer #(.select(2), .enable("false")) multiplexer_2 (
    .in0(Cin_2), .in1(not_1_out), .in2(not_1_out), .in3(Cin_2), .out(Sum), .sel({B_2, A_2}));
endmodule
