// Logisim project Minority Circuit.circ as structural Verilog: 1 circuit, main circuit main
module main (
  input  z,
  input  y,
  input  x,
  output Majority
);

  Multiplexer #(.select(2), .enable("false")) multiplexer_1 (
    .in0(1'b0), .in1(z), .in2(z), .in3(1'b1), .out(Majority), .sel({x, y}));

  // Notes on the sheet:
  //   Majority Circuit
endmodule
