// Logisim project State Machines.circ as structural Verilog: 1 circuit, main circuit main
module main (
  input  [1:0] state,
  input  \input ,
  output [1:0] next
);

  wire or_1_out, or_2_out;

  or or_1 (or_1_out, state[0], \input );
  or or_2 (or_2_out, state[0], \input );
  not not_1 (next[0], \input );
  Multiplexer multiplexer_1 (.in0(or_1_out), .in1(or_2_out), .out(next[1]), .sel(state[1]));  // open: en
endmodule
