// Logisim project Weird State Machine lab 6.circ as structural Verilog: 2 circuits, main circuit main
module main (
  input  in_1
);

  wire clock_1_out;
  wire [1:0] lab6example_1_next, register_1_q;

  lab6example lab6example_1 (.State(register_1_q), .\input (in_1), .next(lab6example_1_next));
  Clock clock_1 (.out(clock_1_out));
  Register #(.width(2)) register_1 (.D(lab6example_1_next), .Q(register_1_q), .clr(clock_1_out));  // open: en, clk
endmodule

module lab6example (
  input  [1:0] State,
  input  \input ,
  output [1:0] next
);

  wire and_1_out, and_2_out, and_3_out, and_4_out, not_1_out, not_2_out, not_3_out, or_1_out, or_2_out,
       xor_1_out;

  not not_1 (not_1_out, State[0]);
  not not_2 (not_2_out, State[1]);
  not not_3 (not_3_out, \input );
  and and_1 (and_1_out, not_2_out, State[0]);
  xor xor_1 (xor_1_out, \input , State[0]);
  or or_1 (or_1_out, not_1_out, not_3_out);
  and and_2 (and_2_out, xor_1_out, State[1]);
  and and_3 (and_3_out, not_2_out, or_1_out);
  or or_2 (or_2_out, not_1_out, \input );
  and and_4 (and_4_out, State[1], or_2_out);
  or or_3 (next[1], and_1_out, and_2_out);
  or or_4 (next[0], and_3_out, and_4_out);
endmodule
